# Fritzing sketch cloud_lamp (saved by Fritzing 0.8.7b)
breadboards: 1

parts:
  元件1 = Arduino Nano (Rev3.0)
  元件2 = Bluetooth Mate Silver
  元件3 = Breakout Board for Electret Microphone
  U1 = Voltage Regulator - 5V [package="TO220 [THT]"]
  C1 = Electrolytic Capacitor [capacitance=1µF package="100 mil [THT, electrolytic]"]
  C2 = Electrolytic Capacitor [capacitance=1µF package="100 mil [THT, electrolytic]"]
  Power_plug1 = Power plug

nets:
  GND: 元件1.GND, 元件2.GND, 元件3.GND, U1.GND, C1.-, C2.-, Power_plug1.GND
  N1: 元件1.D2, 元件2.TX_5V
  N2: 元件1.D4, 元件2.RTS_5V
  ws2812_DIN: 元件1.D6
  VIN: 元件1.VIN, U1.input_voltage, C1.+, Power_plug1.VCC
  5V: 元件1.5V, 元件3.VCC
  N3: 元件1.A0, 元件3.AUD
  N4: U1.output_voltage, C2.+
